# Fritzing sketch circuit (saved by Fritzing 0.9.3b)
circuit board: 8.46667cm x 5.64444cm
breadboards: 1

parts:
  Part1 = Arduino Nano (Rev3.0) (ICSP)
  U1 = Sharp PC817 [part_number="управление режимом" package=THT]
  U2 = Sharp PC817 [part_number="управление сбросом" package=THT]
  R1 = Resistor [tolerance=±0.05% resistance=10k package="0402 [SMD]"]
  R2 = Resistor [tolerance=±0.05% resistance=10k package="0402 [SMD]"]
  R3 = Resistor [tolerance=±0.05% resistance=1k package="0402 [SMD]"]
  R4 = Resistor [tolerance=±0.05% resistance=1k package="0402 [SMD]"]
  J1 = male pin header, 5 pins [form="♂ (male)"]
  R5 = Resistor [tolerance=±0.05% resistance=6.8k part_number=режим package="0402 [SMD]"]
  R6 = Resistor [tolerance=±0.05% resistance=5k part_number=сброс package="0402 [SMD]"]

nets:
  GND: Part1.GND, Part1.D10, U1.Pin_2, U1.Pin_3, U2.Pin_2, U2.Pin_3, R1.Pin_1, R2.Pin_1, J1.pin4
  N1: Part1.D2, R1.Pin_0, R3.Pin_1
  N2: Part1.D3, R2.Pin_0, R4.Pin_1
  N3: Part1.D11/MOSI, J1.pin2
  N4: Part1.5V, J1.pin5
  N5: Part1.D13/SCK, J1.pin1
  N6: U1.Pin_1, R3.Pin_0
  N7: U1.Pin_4, R5.Pin_1
  N8: U2.Pin_1, R4.Pin_0
  N9: U2.Pin_4, R6.Pin_1
  N10: J1.pin3, R5.Pin_0, R6.Pin_0

notes:
  clock
  data
  gnd
  +5v
  buttons
  - R1, R2 - подтягивают цифровые выходы на землю, для предотвращения появления на них высокого уровня, при подаче питания / перезагрузке
  - R3, R4 - нужны для того чтобы не сгорел диод в оптопаре, номинал нужно подобрать в зависимости от используемой оптопары
  - U1, U2 - оптопары для программного нажатия на кнопки сброса и режима, подойдут любые, я использовал одну сдвоенную
  - R5, R6 - резисторы для программного нажатия на кнопки сброса и режима, нужно подобрать что нибудь +/- близкое
